// Logisim project alu.circ as structural Verilog: 13 circuits, main circuit main
module main (
  input  [31:0] X,
  input  [31:0] Y,
  input  [3:0] Switch,
  output Signed_Overflow,
  output Equal,
  output [31:0] Result
);

  wire [31:0] demultiplexer_1_out0, demultiplexer_1_out2, demultiplexer_1_out3, demultiplexer_1_out4,
       demultiplexer_1_out5, demultiplexer_1_out6, demultiplexer_1_out7, demultiplexer_1_out8,
       demultiplexer_1_out9, demultiplexer_1_out10, demultiplexer_1_out11, demultiplexer_1_out12,
       demultiplexer_2_out0, demultiplexer_2_out1, demultiplexer_2_out2, demultiplexer_2_out3,
       demultiplexer_2_out4, demultiplexer_2_out5, demultiplexer_2_out6, demultiplexer_2_out7,
       demultiplexer_2_out8, demultiplexer_2_out9, demultiplexer_2_out10, demultiplexer_2_out11;

  Demultiplexer #(.select(4), .width(32), .enable("false")) demultiplexer_1 (
    .out0(demultiplexer_1_out0), .out2(demultiplexer_1_out2), .out3(demultiplexer_1_out3),
    .out4(demultiplexer_1_out4), .out5(demultiplexer_1_out5), .out6(demultiplexer_1_out6),
    .out7(demultiplexer_1_out7), .out8(demultiplexer_1_out8), .out9(demultiplexer_1_out9),
    .out10(demultiplexer_1_out10), .out11(demultiplexer_1_out11), .out12(demultiplexer_1_out12), .in(X),
    .sel(Switch));  // open: out1, out13, out14, out15
  Demultiplexer #(.select(4), .width(32), .enable("false")) demultiplexer_2 (
    .out0(demultiplexer_2_out0), .out1(demultiplexer_2_out1), .out2(demultiplexer_2_out2),
    .out3(demultiplexer_2_out3), .out4(demultiplexer_2_out4), .out5(demultiplexer_2_out5),
    .out6(demultiplexer_2_out6), .out7(demultiplexer_2_out7), .out8(demultiplexer_2_out8),
    .out9(demultiplexer_2_out9), .out10(demultiplexer_2_out10), .out11(demultiplexer_2_out11), .in(Y),
    .sel(Switch));  // open: out12, out13, out14, out15
  sll sll (
    .X(demultiplexer_1_out0), .Y(demultiplexer_2_out0), .Signed_Overflow(Signed_Overflow), .Equal(Equal),
    .Result(Result));
  srl srl (
    .X(demultiplexer_1_out2), .Y(demultiplexer_2_out1), .Signed_Overflow(Signed_Overflow), .Equal(Equal),
    .Result(Result));
  sra sra (
    .X(demultiplexer_1_out3), .Y(demultiplexer_2_out2), .Signed_Overflow(Signed_Overflow), .Equal(Equal),
    .Result(Result));
  add add (
    .X(demultiplexer_1_out4), .Y(demultiplexer_2_out3), .Signed_Overflow(Signed_Overflow), .Equal(Equal),
    .Result(Result));
  addu addu (
    .X(demultiplexer_1_out5), .Y(demultiplexer_2_out4), .Signed_Overflow(Signed_Overflow), .Equal(Equal),
    .Result(Result));
  sub sub (
    .X(demultiplexer_1_out6), .Y(demultiplexer_2_out5), .Signed_Overflow(Signed_Overflow), .Equal(Equal),
    .Result(Result));
  subu subu (
    .X(demultiplexer_1_out7), .Y(demultiplexer_2_out6), .Signed_Overflow(Signed_Overflow), .Equal(Equal),
    .Result(Result));
  \and  \and  (
    .X(demultiplexer_1_out8), .Y(demultiplexer_2_out7), .Signed_Overflow(Signed_Overflow), .Equal(Equal),
    .Result(Result));
  \or  \or  (
    .X(demultiplexer_1_out9), .Y(demultiplexer_2_out8), .Signed_Overflow(Signed_Overflow), .Equal(Equal),
    .Result(Result));
  \xor  \xor  (
    .X(demultiplexer_1_out10), .Y(demultiplexer_2_out9), .Signed_Overflow(Signed_Overflow), .Equal(Equal),
    .Result(Result));
  slt slt (
    .X(demultiplexer_1_out11), .Y(demultiplexer_2_out10), .Signed_Overflow(Signed_Overflow), .Equal(Equal),
    .Result(Result));
  sltu slt_2 (
    .X(demultiplexer_1_out12), .Y(demultiplexer_2_out11), .Signed_Overflow(Signed_Overflow), .Equal(Equal),
    .Result(Result));

  // Other names for the same wires on the sheet: overflow = Signed_Overflow; S[3:0] = Switch

  // Notes on the sheet:
  //   INPUTS to your circuit
  //   X = first operand
  //   Switch = determine action
  //   Y = second operand
  //   DON'T CHANGE THE LOCATIONS OF THE INPUTS AND OUTPUTS!
  //   Switch Key:
  //   0 | sll | Y << X | 0
  //   4 | addu | X + Y | 0
  //   6 | subu | X - Y | 0
  //   8 | or | X OR Y | 0
  //   OUTPUTS from your circuit
  //   Equal : 1 iff X==Y
  //   Result = result of op
  //   2 | sra | Y >>> X | 0
  //   SignO: 1 iff operation +/- and there was signO
  //   Switch | Operation Name | Result | Signed Overflow
  //   1 | srl | Y >> X | 0
  //   10 | slt (signed comp) | ( X < Y) ? 1 : 0 | 0
  //   11 | sltu (unsighed comp) | (X < Y) ? 1 : 0 | 0
  //   slt == 0xFFFFFFFF < 0x0000000 is 1
  //   sltu == 0xFFFFFFFF < 0x00000000 is 0
  //   3 | add | X + Y | 1 iff overflow
  //   5 | sub | X - Y | 1 iff overflow
  //   7 | and | X AND Y | 0
  //   9 | xor | X XOR Y | 0
endmodule

module sll (
  input  [31:0] X,
  input  [31:0] Y,
  output Signed_Overflow,
  output Equal,
  output [31:0] Result
);

  Shifter #(.width(32)) shifter_1 (.in(Y), .\dist (X[4:0]), .out(Result));
  Comparator #(.width(32)) comparator_1 (.a(Y), .b(X), .eq(Equal));  // open: gt, lt

  assign Signed_Overflow = 1'b0;

  // Notes on the sheet:
  //   INPUTS to your circuit
  //   OUTPUTS from your circuit
endmodule

module srl (
  input  [31:0] X,
  input  [31:0] Y,
  output Signed_Overflow,
  output Equal,
  output [31:0] Result
);

  Shifter #(.width(32), .shift("lr")) shifter_1 (.in(Y), .\dist (X[4:0]), .out(Result));
  Comparator #(.width(32)) comparator_1 (.a(Y), .b(X), .eq(Equal));  // open: gt, lt

  assign Signed_Overflow = 1'b0;

  // Notes on the sheet:
  //   INPUTS to your circuit
  //   OUTPUTS from your circuit
endmodule

module sra (
  input  [31:0] X,
  input  [31:0] Y,
  output Signed_Overflow,
  output Equal,
  output [31:0] Result
);

  Shifter #(.width(32), .shift("ar")) shifter_1 (.in(Y), .\dist (X[4:0]), .out(Result));
  Comparator #(.width(32)) comparator_1 (.a(Y), .b(X), .eq(Equal));  // open: gt, lt

  assign Signed_Overflow = 1'b0;

  // Notes on the sheet:
  //   INPUTS to your circuit
  //   OUTPUTS from your circuit
endmodule

module add (
  input  [31:0] X,
  input  [31:0] Y,
  output Signed_Overflow,
  output Equal,
  output [31:0] Result
);

  Adder #(.width(32)) adder_1 (.a(X), .b(Y), .out(Result), .cout(Signed_Overflow));  // open: cin
  Comparator #(.width(32)) comparator_1 (.a(X), .b(Y), .eq(Equal));  // open: gt, lt

  // Notes on the sheet:
  //   INPUTS to your circuit
  //   OUTPUTS from your circuit
endmodule

module addu (
  input  [31:0] X,
  input  [31:0] Y,
  output Signed_Overflow,
  output Equal,
  output [31:0] Result
);

  Adder #(.width(32)) adder_1 (.a(X), .b(Y), .out(Result));  // open: cin, cout
  Comparator #(.width(32)) comparator_1 (.a(X), .b(Y), .eq(Equal));  // open: gt, lt

  assign Signed_Overflow = 1'b0;

  // Notes on the sheet:
  //   INPUTS to your circuit
  //   OUTPUTS from your circuit
endmodule

module sub (
  input  [31:0] X,
  input  [31:0] Y,
  output Signed_Overflow,
  output Equal,
  output [31:0] Result
);

  wire [31:0] negator_1_out;

  Negator #(.width(32)) negator_1 (.in(Y), .out(negator_1_out));
  Adder #(.width(32)) adder_1 (.a(X), .b(negator_1_out), .out(Result), .cout(Signed_Overflow));  // open: cin
  Comparator #(.width(32)) comparator_1 (.a(X), .b(Y), .eq(Equal));  // open: gt, lt

  // Notes on the sheet:
  //   INPUTS to your circuit
  //   OUTPUTS from your circuit
endmodule

module subu (
  input  [31:0] X,
  input  [31:0] Y,
  output Signed_Overflow,
  output Equal,
  output [31:0] Result
);

  wire [31:0] negator_1_out;

  Negator #(.width(32)) negator_1 (.in(Y), .out(negator_1_out));
  Adder #(.width(32)) adder_1 (.a(X), .b(negator_1_out), .out(Result));  // open: cin, cout
  Comparator #(.width(32)) comparator_1 (.a(X), .b(Y), .eq(Equal));  // open: gt, lt

  assign Signed_Overflow = 1'b0;

  // Notes on the sheet:
  //   INPUTS to your circuit
  //   OUTPUTS from your circuit
endmodule

module \and  (
  input  [31:0] X,
  input  [31:0] Y,
  output Signed_Overflow,
  output Equal,
  output [31:0] Result
);

  assign Result = X & Y;  // AND_Gate and_1, 32 bits wide
  Comparator #(.width(32)) comparator_1 (.a(X), .b(Y), .eq(Equal));  // open: gt, lt

  assign Signed_Overflow = 1'b0;

  // Notes on the sheet:
  //   INPUTS to your circuit
  //   OUTPUTS from your circuit
endmodule

module \or  (
  input  [31:0] X,
  input  [31:0] Y,
  output Signed_Overflow,
  output Equal,
  output [31:0] Result
);

  Comparator #(.width(32)) comparator_1 (.a(X), .b(Y), .eq(Equal));  // open: gt, lt
  assign Result = X | Y;  // OR_Gate or_1, 32 bits wide

  assign Signed_Overflow = 1'b0;

  // Notes on the sheet:
  //   INPUTS to your circuit
  //   OUTPUTS from your circuit
endmodule

module \xor  (
  input  [31:0] X,
  input  [31:0] Y,
  output Signed_Overflow,
  output Equal,
  output [31:0] Result
);

  Comparator #(.width(32)) comparator_1 (.a(X), .b(Y), .eq(Equal));  // open: gt, lt
  assign Result = X ^ Y;  // XOR_Gate xor_1, 32 bits wide

  assign Signed_Overflow = 1'b0;

  // Notes on the sheet:
  //   INPUTS to your circuit
  //   OUTPUTS from your circuit
endmodule

module slt (
  input  [31:0] X,
  input  [31:0] Y,
  output Signed_Overflow,
  output Equal,
  output [31:0] Result
);

  Comparator #(.width(32)) comparator_1 (.a(X), .b(Y), .eq(Equal), .lt(Result[0]));  // open: gt

  assign Result[31:1] = {31{1'b0}};
  assign Signed_Overflow = 1'b0;

  // Notes on the sheet:
  //   INPUTS to your circuit
  //   OUTPUTS from your circuit
endmodule

module sltu (
  input  [31:0] X,
  input  [31:0] Y,
  output Signed_Overflow,
  output Equal,
  output [31:0] Result
);

  Comparator #(.width(32), .mode("unsigned")) comparator_1 (.a(X), .b(Y), .eq(Equal), .lt(Result[0]));  // open: gt

  assign Result[31:1] = {31{1'b0}};
  assign Signed_Overflow = 1'b0;

  // Notes on the sheet:
  //   INPUTS to your circuit
  //   OUTPUTS from your circuit
endmodule
