// Logisim project regfile.circ as structural Verilog: 3 circuits, main circuit main
module main (
  input  [4:0] Read_Register_1,
  input  [4:0] Read_Register_2,
  input  [4:0] Write_Register,
  input  [31:0] Write_Data,
  input  Write_Enable,
  input  Clock,
  output [31:0] s0_Value,
  output [31:0] s1_Value,
  output [31:0] s2_Value,
  output [31:0] ra_Value,
  output [31:0] sp_Value,
  output [31:0] Read_Data_1,
  output [31:0] Read_Data_2
);

  regfile regfile_1 (
    .write_register(Write_Register), .write_enable(Write_Enable), .in_4(Write_Data),
    .read_register_1(Read_Register_2), .Read1(Read_Data_1), .read_register_2(Read_Register_1),
    .Read2(Read_Data_2), .ra(ra_Value), .sp(sp_Value), .S2(s2_Value), .S1(s1_Value), .S0(s0_Value),
    .clock(Clock));

  // Other names for the same wires on the sheet: clk = Clock; read_data1[31:0] = Read_Data_1;
  //   read_data2[31:0] = Read_Data_2; read_reg1[4:0] = Read_Register_1; read_reg2[4:0] = Read_Register_2;
  //   write_en = Write_Enable; write_reg[4:0] = Write_Register

  // Notes on the sheet:
  //   INPUTS to your circuit
  //   DON'T CHANGE THE LOCATIONS OF THE INPUTS AND OUTPUTS!
  //   These are DEBUG/TEST outputs from your circuit.
  //   OUTPUTS from your circuit
endmodule

module gated_register (
  input  [31:0] \input ,
  input  writelocal,
  input  clock,
  output [31:0] \output 
);

  wire [31:0] multiplexer_1_out;

  Multiplexer #(.width(32)) multiplexer_1 (
    .in0(\output ), .in1(\input ), .out(multiplexer_1_out), .sel(writelocal));  // open: en
  Register #(.width(32)) register_1 (.D(multiplexer_1_out), .Q(\output ), .clk(clock));  // open: en, clr
endmodule

module regfile (
  input  [4:0] read_register_2,
  input  [4:0] read_register_1,
  input  clock,
  input  [31:0] in_4,
  input  [4:0] write_register,
  input  write_enable,
  output [31:0] ra,
  output [31:0] sp,
  output [31:0] S2,
  output [31:0] S1,
  output [31:0] S0,
  output [31:0] Read1,
  output [31:0] Read2
);

  wire decoder_1_out0, decoder_1_out1, decoder_1_out2, decoder_1_out3, decoder_1_out4, decoder_1_out5,
       decoder_1_out6, decoder_1_out7, decoder_1_out8, decoder_1_out9, decoder_1_out10, decoder_1_out11,
       decoder_1_out12, decoder_1_out13, decoder_1_out14, decoder_1_out15, decoder_1_out16, decoder_1_out17,
       decoder_1_out18, decoder_1_out19, decoder_1_out20, decoder_1_out21, decoder_1_out22, decoder_1_out23,
       decoder_1_out24, decoder_1_out25, decoder_1_out26, decoder_1_out27, decoder_1_out28, decoder_1_out29,
       decoder_1_out30, decoder_1_out31;
  wire [31:0] gated_register_1_output, gated_register_2_output, gated_register_3_output,
       gated_register_4_output, gated_register_5_output, gated_register_6_output, gated_register_7_output,
       gated_register_8_output, gated_register_9_output, gated_register_10_output, gated_register_11_output,
       gated_register_12_output, gated_register_13_output, gated_register_14_output,
       gated_register_15_output, gated_register_19_output, gated_register_20_output,
       gated_register_21_output, gated_register_22_output, gated_register_23_output,
       gated_register_24_output, gated_register_25_output, gated_register_26_output,
       gated_register_27_output, gated_register_28_output, gated_register_30_output;

  gated_register gated_register_1 (
    .\input (in_4), .writelocal(decoder_1_out1), .clock(clock), .\output (gated_register_1_output));
  gated_register gated_register_2 (
    .\input (in_4), .writelocal(decoder_1_out2), .clock(clock), .\output (gated_register_2_output));
  gated_register gated_register_3 (
    .\input (in_4), .writelocal(decoder_1_out3), .clock(clock), .\output (gated_register_3_output));
  gated_register gated_register_4 (
    .\input (in_4), .writelocal(decoder_1_out4), .clock(clock), .\output (gated_register_4_output));
  gated_register gated_register_5 (
    .\input (in_4), .writelocal(decoder_1_out5), .clock(clock), .\output (gated_register_5_output));
  gated_register gated_register_6 (
    .\input (in_4), .writelocal(decoder_1_out6), .clock(clock), .\output (gated_register_6_output));
  gated_register gated_register_7 (
    .\input (in_4), .writelocal(decoder_1_out7), .clock(clock), .\output (gated_register_7_output));
  gated_register gated_register_8 (
    .\input (in_4), .writelocal(decoder_1_out8), .clock(clock), .\output (gated_register_8_output));
  gated_register gated_register_9 (
    .\input (in_4), .writelocal(decoder_1_out9), .clock(clock), .\output (gated_register_9_output));
  gated_register gated_register_10 (
    .\input (in_4), .writelocal(decoder_1_out10), .clock(clock), .\output (gated_register_10_output));
  gated_register gated_register_11 (
    .\input (in_4), .writelocal(decoder_1_out11), .clock(clock), .\output (gated_register_11_output));
  Decoder #(.select(5), .disabled(0)) decoder_1 (
    .out0(decoder_1_out0), .out1(decoder_1_out1), .out2(decoder_1_out2), .out3(decoder_1_out3),
    .out4(decoder_1_out4), .out5(decoder_1_out5), .out6(decoder_1_out6), .out7(decoder_1_out7),
    .out8(decoder_1_out8), .out9(decoder_1_out9), .out10(decoder_1_out10), .out11(decoder_1_out11),
    .out12(decoder_1_out12), .out13(decoder_1_out13), .out14(decoder_1_out14), .out15(decoder_1_out15),
    .out16(decoder_1_out16), .out17(decoder_1_out17), .out18(decoder_1_out18), .out19(decoder_1_out19),
    .out20(decoder_1_out20), .out21(decoder_1_out21), .out22(decoder_1_out22), .out23(decoder_1_out23),
    .out24(decoder_1_out24), .out25(decoder_1_out25), .out26(decoder_1_out26), .out27(decoder_1_out27),
    .out28(decoder_1_out28), .out29(decoder_1_out29), .out30(decoder_1_out30), .out31(decoder_1_out31),
    .sel(write_register), .en(write_enable));
  gated_register gated_register_12 (
    .\input (in_4), .writelocal(decoder_1_out12), .clock(clock), .\output (gated_register_12_output));
  gated_register gated_register_13 (
    .\input (in_4), .writelocal(decoder_1_out13), .clock(clock), .\output (gated_register_13_output));
  gated_register gated_register_14 (
    .\input (in_4), .writelocal(decoder_1_out14), .clock(clock), .\output (gated_register_14_output));
  gated_register gated_register_15 (
    .\input (in_4), .writelocal(decoder_1_out15), .clock(clock), .\output (gated_register_15_output));
  gated_register gated_register_16 (.\input (in_4), .writelocal(decoder_1_out16), .clock(clock), .\output (S0));
  gated_register gated_register_17 (.\input (in_4), .writelocal(decoder_1_out17), .clock(clock), .\output (S1));
  gated_register gated_register_18 (.\input (in_4), .writelocal(decoder_1_out18), .clock(clock), .\output (S2));
  gated_register gated_register_19 (
    .\input (in_4), .writelocal(decoder_1_out19), .clock(clock), .\output (gated_register_19_output));
  gated_register gated_register_20 (
    .\input (in_4), .writelocal(decoder_1_out20), .clock(clock), .\output (gated_register_20_output));
  gated_register gated_register_21 (
    .\input (in_4), .writelocal(decoder_1_out21), .clock(clock), .\output (gated_register_21_output));
  gated_register gated_register_22 (
    .\input (in_4), .writelocal(decoder_1_out22), .clock(clock), .\output (gated_register_22_output));
  gated_register gated_register_23 (
    .\input (in_4), .writelocal(decoder_1_out23), .clock(clock), .\output (gated_register_23_output));
  gated_register gated_register_24 (
    .\input (in_4), .writelocal(decoder_1_out24), .clock(clock), .\output (gated_register_24_output));
  gated_register gated_register_25 (
    .\input (in_4), .writelocal(decoder_1_out25), .clock(clock), .\output (gated_register_25_output));
  gated_register gated_register_26 (
    .\input (in_4), .writelocal(decoder_1_out26), .clock(clock), .\output (gated_register_26_output));
  gated_register gated_register_27 (
    .\input (in_4), .writelocal(decoder_1_out27), .clock(clock), .\output (gated_register_27_output));
  gated_register gated_register_28 (
    .\input (in_4), .writelocal(decoder_1_out28), .clock(clock), .\output (gated_register_28_output));
  gated_register gated_register_29 (.\input (in_4), .writelocal(decoder_1_out29), .clock(clock), .\output (sp));
  gated_register gated_register_30 (
    .\input (in_4), .writelocal(decoder_1_out30), .clock(clock), .\output (gated_register_30_output));
  gated_register gated_register_31 (.\input (in_4), .writelocal(decoder_1_out31), .clock(clock), .\output (ra));
  Multiplexer #(.select(5), .width(32)) multiplexer_1 (
    .in0({32{1'b0}}), .in1(gated_register_1_output), .in2(gated_register_2_output),
    .in3(gated_register_3_output), .in4(gated_register_4_output), .in5(gated_register_5_output),
    .in6(gated_register_6_output), .in7(gated_register_7_output), .in8(gated_register_8_output),
    .in9(gated_register_9_output), .in10(gated_register_10_output), .in11(gated_register_11_output),
    .in12(gated_register_12_output), .in13(gated_register_13_output), .in14(gated_register_14_output),
    .in15(gated_register_15_output), .in16(S0), .in17(S1), .in18(S2), .in19(gated_register_19_output),
    .in20(gated_register_20_output), .in21(gated_register_21_output), .in22(gated_register_22_output),
    .in23(gated_register_23_output), .in24(gated_register_24_output), .in25(gated_register_25_output),
    .in26(gated_register_26_output), .in27(gated_register_27_output), .in28(gated_register_28_output),
    .in29(sp), .in30(gated_register_30_output), .in31(ra), .out(Read1), .sel(read_register_1));  // open: en
  Multiplexer #(.select(5), .width(32)) multiplexer_2 (
    .in0({32{1'b0}}), .in1(gated_register_1_output), .in2(gated_register_2_output),
    .in3(gated_register_3_output), .in4(gated_register_4_output), .in5(gated_register_5_output),
    .in6(gated_register_6_output), .in7(gated_register_7_output), .in8(gated_register_8_output),
    .in9(gated_register_9_output), .in10(gated_register_10_output), .in11(gated_register_11_output),
    .in12(gated_register_12_output), .in13(gated_register_13_output), .in14(gated_register_14_output),
    .in15(gated_register_15_output), .in16(S0), .in17(S1), .in18(S2), .in19(gated_register_19_output),
    .in20(gated_register_20_output), .in21(gated_register_21_output), .in22(gated_register_22_output),
    .in23(gated_register_23_output), .in24(gated_register_24_output), .in25(gated_register_25_output),
    .in26(gated_register_26_output), .in27(gated_register_27_output), .in28(gated_register_28_output),
    .in29(sp), .in30(gated_register_30_output), .in31(ra), .out(Read2), .sel(read_register_2));  // open: en
endmodule
