// Logisim project alu-sub.circ as structural Verilog: 1 circuit, main circuit main
module main (
  output [7:0] Test_num,
  output Signed_Overflow,
  output Equal,
  output [31:0] Result
);

  wire clock_1_out;
  wire [3:0] rom_3_data;
  wire [7:0] adder_1_out;
  wire [31:0] rom_1_data, rom_2_data;

  Clock clock_1 (.out(clock_1_out));
  Adder adder_1 (.a(8'h1), .b(Test_num), .out(adder_1_out));  // open: cin, cout
  Register register_1 (.D(adder_1_out), .Q(Test_num), .clk(clock_1_out));  // open: en, clr
  ROM #(.dataWidth(32)) rom_1 (.addr(Test_num), .data(rom_1_data));  // open: sel
  ROM #(.dataWidth(32)) rom_2 (.addr(Test_num), .data(rom_2_data));  // open: sel
  ROM #(.dataWidth(4)) rom_3 (.addr(Test_num), .data(rom_3_data));  // open: sel
  alu_main main_1 (
    .Switch(rom_3_data), .X(rom_1_data), .Equal(Equal), .Result(Result), .Signed_Overflow(Signed_Overflow),
    .Y(rom_2_data));

  // Notes on the sheet:
  //   contents of rom_1 (hex, n*v repeats v):
  //   ffff 0 80000000 70000000 abcd 12345678 11111111 ffff
  //   contents of rom_2 (hex, n*v repeats v):
  //   7fffffff 8ffffff fffffff afffffff cd 10000000 1010101 ffff
  //   contents of rom_3 (hex, n*v repeats v):
  //   32*5
  //   YOUR ALU SHOULD FIT HERE
  //   There should be no blue/red wires here, and the result shouldn't be x's.
endmodule
