// Logisim project cpu.circ as structural Verilog: 11 circuits, main circuit main
module main (
  input  [31:0] INSTRUCTION,
  input  CLOCK,
  output [31:0] FETCH_ADDRESS,
  output [31:0] s0_Value,
  output [31:0] s1_Value,
  output [31:0] s2_Value,
  output [31:0] ra_Value,
  output [31:0] sp_Value
);

  wire alusrc, and_4_out, and_6_out, branch, comparator_1_do_branch, comparator_2_lt, comparator_4_eq,
       comparator_5_eq, d_write, decoder_1_out0, decoder_1_out1, decoder_1_out2, decoder_1_out3,
       decoder_1_out4, decoder_1_out5, decoder_1_out6, decoder_1_out7, decoder_1_out8, decoder_1_out9,
       decoder_1_out10, decoder_1_out11, decoder_1_out12, decoder_1_out13, decoder_1_out14, decoder_1_out15,
       decoder_1_out16, decoder_1_out17, decoder_1_out18, decoder_1_out19, decoder_1_out20, decoder_1_out21,
       decoder_1_out22, decoder_1_out23, decoder_1_out24, decoder_1_out25, decoder_1_out26, decoder_1_out27,
       decoder_1_out28, decoder_1_out29, decoder_1_out30, decoder_1_out31, jump, link, logical, lui,
       memtoreg, memwrite, not_1_out, not_2_out, pc_src, regdst, regwrite, shift, use_display, use_jloc, zero;
  wire [3:0] alucontrol;
  wire [4:0] d_addr, multiplexer_1_out, multiplexer_2_out;
  wire [23:0] demultiplexer_1_out0, demultiplexer_1_out1;
  wire [31:0] adder_1_out, alu_x, alu_y, bit_extender_2_out, bit_extender_3_out, d_out, demultiplexer_2_out0,
       demultiplexer_2_out1, demultiplexer_2_out2, demultiplexer_2_out3, demultiplexer_2_out4,
       demultiplexer_2_out5, demultiplexer_2_out6, demultiplexer_2_out7, demultiplexer_2_out8,
       demultiplexer_2_out9, demultiplexer_2_out10, demultiplexer_2_out11, demultiplexer_2_out12,
       demultiplexer_2_out13, demultiplexer_2_out14, demultiplexer_2_out15, demultiplexer_2_out16,
       demultiplexer_2_out17, demultiplexer_2_out18, demultiplexer_2_out19, demultiplexer_2_out20,
       demultiplexer_2_out21, demultiplexer_2_out22, demultiplexer_2_out23, demultiplexer_2_out24,
       demultiplexer_2_out25, demultiplexer_2_out26, demultiplexer_2_out27, demultiplexer_2_out28,
       demultiplexer_2_out29, demultiplexer_2_out30, demultiplexer_2_out31, display_control_1_outval,
       display_control_1_outval_2, display_control_1_outval_3, display_control_1_outval_4,
       display_control_1_outval_5, display_control_1_outval_6, display_control_1_outval_7,
       display_control_1_outval_8, display_control_1_outval_9, display_control_1_outval_10,
       display_control_1_outval_11, display_control_1_outval_12, display_control_1_outval_13,
       display_control_1_outval_14, display_control_1_outval_15, display_control_1_outval_16,
       display_control_1_outval_17, display_control_1_outval_18, display_control_1_outval_19,
       display_control_1_outval_20, display_control_1_outval_21, display_control_1_outval_22,
       display_control_1_outval_23, display_control_1_outval_24, display_control_1_outval_25,
       display_control_1_outval_26, display_control_1_outval_27, display_control_1_outval_28,
       display_control_1_outval_29, display_control_1_outval_30, display_control_1_outval_31,
       display_control_1_outval_32, imm, jloc, main_1_result, multiplexer_3_out, multiplexer_7_out,
       multiplexer_8_out, multiplexer_9_out, multiplexer_10_out, ram_1_data, RegisterFile_read1, shamt, ui;

  comparator comparator_1 (.opcode(INSTRUCTION[31:26]), .alu1(alu_x), .alu2(alu_y), .do_branch(comparator_1_do_branch));
  Multiplexer #(.width(5), .enable("false")) multiplexer_1 (
    .in0(multiplexer_2_out), .in1({5{1'b1}}), .out(multiplexer_1_out), .sel(link));
  Multiplexer #(.width(5), .enable("false")) multiplexer_2 (
    .in0(INSTRUCTION[20:16]), .in1(INSTRUCTION[15:11]), .out(multiplexer_2_out), .sel(regdst));
  pc_control pc_control_1 (
    .fetch_addr(FETCH_ADDRESS), .imm(jloc), .instr(INSTRUCTION), .usejloc(use_jloc), .pc_src(pc_src),
    .jump(jump), .clock(CLOCK), .fetch_addr_2(FETCH_ADDRESS));
  and and_1 (pc_src, branch, comparator_1_do_branch);
  assign shamt = {{27{1'b0}}, INSTRUCTION[10:6]};  // Bit_Extender bit_extender_1
  // Probe on INSTRUCTION
  regfile RegisterFile (
    .write_register(multiplexer_1_out), .write_enable(regwrite), .wIn(multiplexer_7_out),
    .read_register_1(INSTRUCTION[25:21]), .Read1(RegisterFile_read1), .read_register_2(INSTRUCTION[20:16]),
    .Read2(alu_y), .ra(ra_Value), .sp(sp_Value), .S2(s2_Value), .S1(s1_Value), .S0(s0_Value), .clock(CLOCK));
  logical logical_1 (
    .opcode1(INSTRUCTION[26]), .opcode2(INSTRUCTION[27]), .opcode3(INSTRUCTION[28]),
    .opcode4(INSTRUCTION[29]), .opcode5(INSTRUCTION[30]), .opcode6(INSTRUCTION[31]), .logical(logical));
  assign bit_extender_2_out = {{16{INSTRUCTION[15]}}, INSTRUCTION[15:0]};  // Bit_Extender bit_extender_2
  assign bit_extender_3_out = {{16{1'b0}}, INSTRUCTION[15:0]};  // Bit_Extender bit_extender_3
  ControlUnit controlunit_1 (
    .Opcode(INSTRUCTION[31:26]), .Funct(INSTRUCTION[5:0]), .RegWrite(regwrite), .RegDst(regdst),
    .ALUSrc(alusrc), .Branch(branch), .MemWrite(memwrite), .MemToReg(memtoreg), .jump(jump), .link(link),
    .ALUControl(alucontrol));
  Multiplexer #(.width(32), .enable("false")) multiplexer_3 (
    .in0(RegisterFile_read1), .in1(imm), .out(multiplexer_3_out), .sel(alusrc));
  Multiplexer #(.width(32), .enable("false")) multiplexer_4 (
    .in0(multiplexer_3_out), .in1(shamt), .out(alu_x), .sel(shift));
  Multiplexer #(.width(32), .enable("false")) multiplexer_5 (
    .in0(bit_extender_2_out), .in1(bit_extender_3_out), .out(imm), .sel(logical));
  Comparator #(.width(4), .mode("unsigned")) comparator_2 (
    .a(alucontrol), .b(4'b0011), .lt(comparator_2_lt));  // open: gt, eq
  Comparator #(.width(6)) comparator_3 (.a(INSTRUCTION[31:26]), .b(6'b001111), .eq(lui));  // open: gt, lt
  not not_1 (not_1_out, lui);
  alu_main main_1 (
    .Switch(alucontrol), .X(alu_x), .Equal(zero),
    .Result({main_1_result[31:25], use_display, main_1_result[23:0]}), .Y(alu_y));  // open: Signed_Overflow
  and and_2 (shift, comparator_2_lt, not_1_out);
  Comparator #(.width(6)) comparator_4 (.a(INSTRUCTION[5:0]), .b(6'b001000), .eq(comparator_4_eq));  // open: gt, lt
  Comparator #(.width(6)) comparator_5 (.a(INSTRUCTION[31:26]), .b({6{1'b0}}), .eq(comparator_5_eq));  // open: gt, lt
  Demultiplexer #(.width(24), .enable("false")) demultiplexer_1 (
    .out0(demultiplexer_1_out0), .out1(demultiplexer_1_out1), .in(main_1_result[23:0]), .sel(use_display));
  Multiplexer #(.width(32), .enable("false")) multiplexer_6 (.in0(imm), .in1(alu_x), .out(jloc), .sel(use_jloc));
  and and_3 (use_jloc, comparator_4_eq, comparator_5_eq);
  Bit_Extender #(.in_width(24), .out_width(5), .\type ("sign")) bit_extender_4 (
    .in(demultiplexer_1_out1), .out(d_addr));
  and and_4 (and_4_out, not_2_out, memwrite);
  not not_2 (not_2_out, use_display);
  Multiplexer #(.width(32), .enable("false")) multiplexer_7 (
    .in0(multiplexer_8_out), .in1(ui), .out(multiplexer_7_out), .sel(lui));
  and and_5 (d_write, use_display, memwrite);
  RAM #(.addrWidth(24), .dataWidth(32), .bus("separate")) ram_1 (
    .addr(demultiplexer_1_out0), .din(alu_y), .data(ram_1_data), .str(and_4_out), .clk(CLOCK), .ld(1'b1));  // open: sel, clr
  Multiplexer #(.width(32), .enable("false")) multiplexer_8 (
    .in0(multiplexer_10_out), .in1(adder_1_out), .out(multiplexer_8_out), .sel(link));
  Shifter #(.width(32)) shifter_1 (.in(imm), .\dist (5'b10000), .out(ui));
  Multiplexer #(.width(32), .enable("false")) multiplexer_9 (
    .in0(ram_1_data), .in1(d_out), .out(multiplexer_9_out), .sel(use_display));
  Multiplexer #(.width(32)) multiplexer_10 (
    .in0({main_1_result[31:25], use_display, main_1_result[23:0]}), .in1(multiplexer_9_out),
    .out(multiplexer_10_out), .sel(memtoreg));  // open: en
  Adder #(.width(32)) adder_1 (.a(FETCH_ADDRESS), .b(32'h4), .out(adder_1_out));  // open: cin, cout
  and and_6 (and_6_out, CLOCK, d_write);
  DotMatrix #(.matrixcols(32), .matrixrows(32)) dotmatrix_1 (
    .col0(display_control_1_outval), .col1(display_control_1_outval_2), .col2(display_control_1_outval_3),
    .col3(display_control_1_outval_4), .col4(display_control_1_outval_5), .col5(display_control_1_outval_6),
    .col6(display_control_1_outval_7), .col7(display_control_1_outval_8), .col8(display_control_1_outval_9),
    .col9(display_control_1_outval_10), .col10(display_control_1_outval_11),
    .col11(display_control_1_outval_12), .col12(display_control_1_outval_13),
    .col13(display_control_1_outval_14), .col14(display_control_1_outval_15),
    .col15(display_control_1_outval_16), .col16(display_control_1_outval_17),
    .col17(display_control_1_outval_18), .col18(display_control_1_outval_19),
    .col19(display_control_1_outval_20), .col20(display_control_1_outval_21),
    .col21(display_control_1_outval_22), .col22(display_control_1_outval_23),
    .col23(display_control_1_outval_24), .col24(display_control_1_outval_25),
    .col25(display_control_1_outval_26), .col26(display_control_1_outval_27),
    .col27(display_control_1_outval_28), .col28(display_control_1_outval_29),
    .col29(display_control_1_outval_30), .col30(display_control_1_outval_31),
    .col31(display_control_1_outval_32));
  display_control display_control_1 (
    .inval(demultiplexer_2_out0), .inval_2(demultiplexer_2_out1), .inval_3(demultiplexer_2_out2),
    .inval_4(demultiplexer_2_out3), .inval_5(demultiplexer_2_out4), .inval_6(demultiplexer_2_out5),
    .inval_7(demultiplexer_2_out6), .inval_8(demultiplexer_2_out7), .inval_9(demultiplexer_2_out8),
    .inval_10(demultiplexer_2_out9), .inval_11(demultiplexer_2_out10), .inval_12(demultiplexer_2_out11),
    .inval_13(demultiplexer_2_out12), .inval_14(demultiplexer_2_out13), .inval_15(demultiplexer_2_out14),
    .inval_16(demultiplexer_2_out15), .inval_17(demultiplexer_2_out16), .inval_18(demultiplexer_2_out17),
    .inval_19(demultiplexer_2_out18), .inval_20(demultiplexer_2_out19), .inval_21(demultiplexer_2_out20),
    .inval_22(demultiplexer_2_out21), .inval_23(demultiplexer_2_out22), .inval_24(demultiplexer_2_out23),
    .inval_25(demultiplexer_2_out24), .inval_26(demultiplexer_2_out25), .inval_27(demultiplexer_2_out26),
    .inval_28(demultiplexer_2_out27), .inval_29(demultiplexer_2_out28), .inval_30(demultiplexer_2_out29),
    .inval_31(demultiplexer_2_out30), .inval_32(demultiplexer_2_out31), .outval(display_control_1_outval),
    .outval_2(display_control_1_outval_2), .outval_3(display_control_1_outval_3),
    .outval_4(display_control_1_outval_4), .outval_5(display_control_1_outval_5),
    .outval_6(display_control_1_outval_6), .outval_7(display_control_1_outval_7),
    .outval_8(display_control_1_outval_8), .outval_9(display_control_1_outval_9),
    .outval_10(display_control_1_outval_10), .outval_11(display_control_1_outval_11),
    .outval_12(display_control_1_outval_12), .outval_13(display_control_1_outval_13),
    .outval_14(display_control_1_outval_14), .outval_15(display_control_1_outval_15),
    .outval_16(display_control_1_outval_16), .outval_17(display_control_1_outval_17),
    .outval_18(display_control_1_outval_18), .outval_19(display_control_1_outval_19),
    .outval_20(display_control_1_outval_20), .outval_21(display_control_1_outval_21),
    .outval_22(display_control_1_outval_22), .outval_23(display_control_1_outval_23),
    .outval_24(display_control_1_outval_24), .outval_25(display_control_1_outval_25),
    .outval_26(display_control_1_outval_26), .outval_27(display_control_1_outval_27),
    .outval_28(display_control_1_outval_28), .outval_29(display_control_1_outval_29),
    .outval_30(display_control_1_outval_30), .outval_31(display_control_1_outval_31),
    .outval_32(display_control_1_outval_32), .in_65(and_6_out), .write_4(decoder_1_out31),
    .write_8(decoder_1_out30), .write_12(decoder_1_out29), .write_16(decoder_1_out28),
    .write_20(decoder_1_out27), .write_24(decoder_1_out26), .write_28(decoder_1_out25),
    .write_32(decoder_1_out24), .write_3(decoder_1_out23), .write_7(decoder_1_out22),
    .write_11(decoder_1_out21), .write_15(decoder_1_out20), .write_19(decoder_1_out19),
    .write_23(decoder_1_out18), .write_27(decoder_1_out17), .write_31(decoder_1_out16),
    .write_2(decoder_1_out15), .write_6(decoder_1_out14), .write_10(decoder_1_out13),
    .write_14(decoder_1_out12), .write_18(decoder_1_out11), .write_22(decoder_1_out10),
    .write_26(decoder_1_out9), .write_30(decoder_1_out8), .write(decoder_1_out7), .write_5(decoder_1_out6),
    .write_9(decoder_1_out5), .write_13(decoder_1_out4), .write_17(decoder_1_out3),
    .write_21(decoder_1_out2), .write_25(decoder_1_out1), .write_29(decoder_1_out0));
  Demultiplexer #(.select(5), .width(32), .enable("false")) demultiplexer_2 (
    .out0(demultiplexer_2_out0), .out1(demultiplexer_2_out1), .out2(demultiplexer_2_out2),
    .out3(demultiplexer_2_out3), .out4(demultiplexer_2_out4), .out5(demultiplexer_2_out5),
    .out6(demultiplexer_2_out6), .out7(demultiplexer_2_out7), .out8(demultiplexer_2_out8),
    .out9(demultiplexer_2_out9), .out10(demultiplexer_2_out10), .out11(demultiplexer_2_out11),
    .out12(demultiplexer_2_out12), .out13(demultiplexer_2_out13), .out14(demultiplexer_2_out14),
    .out15(demultiplexer_2_out15), .out16(demultiplexer_2_out16), .out17(demultiplexer_2_out17),
    .out18(demultiplexer_2_out18), .out19(demultiplexer_2_out19), .out20(demultiplexer_2_out20),
    .out21(demultiplexer_2_out21), .out22(demultiplexer_2_out22), .out23(demultiplexer_2_out23),
    .out24(demultiplexer_2_out24), .out25(demultiplexer_2_out25), .out26(demultiplexer_2_out26),
    .out27(demultiplexer_2_out27), .out28(demultiplexer_2_out28), .out29(demultiplexer_2_out29),
    .out30(demultiplexer_2_out30), .out31(demultiplexer_2_out31), .in(alu_y), .sel(d_addr));
  Decoder_part #(.select(5), .enable("false")) decoder_1 (
    .out0(decoder_1_out0), .out1(decoder_1_out1), .out2(decoder_1_out2), .out3(decoder_1_out3),
    .out4(decoder_1_out4), .out5(decoder_1_out5), .out6(decoder_1_out6), .out7(decoder_1_out7),
    .out8(decoder_1_out8), .out9(decoder_1_out9), .out10(decoder_1_out10), .out11(decoder_1_out11),
    .out12(decoder_1_out12), .out13(decoder_1_out13), .out14(decoder_1_out14), .out15(decoder_1_out15),
    .out16(decoder_1_out16), .out17(decoder_1_out17), .out18(decoder_1_out18), .out19(decoder_1_out19),
    .out20(decoder_1_out20), .out21(decoder_1_out21), .out22(decoder_1_out22), .out23(decoder_1_out23),
    .out24(decoder_1_out24), .out25(decoder_1_out25), .out26(decoder_1_out26), .out27(decoder_1_out27),
    .out28(decoder_1_out28), .out29(decoder_1_out29), .out30(decoder_1_out30), .out31(decoder_1_out31),
    .sel(d_addr));
  Multiplexer #(.select(5), .width(32), .enable("false")) multiplexer_11 (
    .in0(display_control_1_outval_32), .in1(display_control_1_outval_31), .in2(display_control_1_outval_30),
    .in3(display_control_1_outval_29), .in4(display_control_1_outval_28), .in5(display_control_1_outval_27),
    .in6(display_control_1_outval_26), .in7(display_control_1_outval_25), .in8(display_control_1_outval_24),
    .in9(display_control_1_outval_23), .in10(display_control_1_outval_22),
    .in11(display_control_1_outval_21), .in12(display_control_1_outval_20),
    .in13(display_control_1_outval_19), .in14(display_control_1_outval_18),
    .in15(display_control_1_outval_17), .in16(display_control_1_outval_16),
    .in17(display_control_1_outval_15), .in18(display_control_1_outval_14),
    .in19(display_control_1_outval_13), .in20(display_control_1_outval_12),
    .in21(display_control_1_outval_11), .in22(display_control_1_outval_10),
    .in23(display_control_1_outval_9), .in24(display_control_1_outval_8), .in25(display_control_1_outval_7),
    .in26(display_control_1_outval_6), .in27(display_control_1_outval_5), .in28(display_control_1_outval_4),
    .in29(display_control_1_outval_3), .in30(display_control_1_outval_2), .in31(display_control_1_outval),
    .out(d_out), .sel(d_addr));

  // Other names for the same wires on the sheet: clk = CLOCK; d_in[31:0] = alu_y; fetch_addr[31:0] = FETCH_ADDRESS;
  //   funct[5:0] = INSTRUCTION[5:0]; opcode[5:0] = INSTRUCTION[31:26]; ra[31:0] = ra_Value; s0[31:0] = s0_Value;
  //   s1[31:0] = s1_Value; s2[31:0] = s2_Value; sp[31:0] = sp_Value

  // Notes on the sheet:
  //   Output
  //   PC Control
  //   These are outputs/inputs from run.circ
  //   Inputs
  //   These are DEBUG/TEST outputs from your circuit.
  //   Control Unit
endmodule

module pc_control (
  input  [31:0] fetch_addr,
  input  [31:0] imm,
  input  pc_src,
  input  jump,
  input  clock,
  input  [31:0] instr,
  input  usejloc,
  output [31:0] fetch_addr_2
);

  wire [31:0] adder_1_out, adder_2_out, multiplexer_1_out, multiplexer_2_out, multiplexer_3_out,
       shifter_1_out, shifter_2_out;

  Shifter #(.width(32)) shifter_1 (.in(instr), .\dist (5'b00010), .out(shifter_1_out));
  Adder #(.width(32)) adder_1 (.a(fetch_addr), .b(32'h4), .out(adder_1_out));  // open: cin, cout
  Adder #(.width(32)) adder_2 (.a(adder_1_out), .b(shifter_2_out), .out(adder_2_out));  // open: cin, cout
  Shifter #(.width(32)) shifter_2 (.in(imm), .\dist (5'b00010), .out(shifter_2_out));
  Multiplexer #(.width(32), .enable("false")) multiplexer_1 (
    .in0({adder_1_out[31:28], shifter_1_out[27:0]}), .in1(imm), .out(multiplexer_1_out), .sel(usejloc));
  Multiplexer #(.width(32)) multiplexer_2 (
    .in0(adder_1_out), .in1(adder_2_out), .out(multiplexer_2_out), .sel(pc_src));  // open: en
  Multiplexer #(.width(32), .enable("false")) multiplexer_3 (
    .in0(multiplexer_2_out), .in1(multiplexer_1_out), .out(multiplexer_3_out), .sel(jump));
  Register #(.width(32)) register_1 (.D(multiplexer_3_out), .Q(fetch_addr_2), .clk(clock));  // open: en, clr
endmodule

module ControlUnit (
  input  [5:0] Opcode,
  input  [5:0] Funct,
  output RegWrite,
  output RegDst,
  output ALUSrc,
  output Branch,
  output MemWrite,
  output MemToReg,
  output jump,
  output link,
  output [3:0] ALUControl
);

  wire and_1_out, comparator_1_eq, comparator_2_eq, decoderpt1_1_jump;
  wire [7:0] ALUOp;

  Comparator #(.width(6)) comparator_1 (.a(Opcode), .b({6{1'b0}}), .eq(comparator_1_eq));  // open: gt, lt
  Comparator #(.width(6), .mode("unsigned")) comparator_2 (
    .a(Funct), .b(6'b001000), .eq(comparator_2_eq));  // open: gt, lt
  DecoderPt1 decoderpt1_1 (
    .Opcode(Opcode[5]), .Opcode2(Opcode[4]), .Opcode3(Opcode[3]), .Opcode4(Opcode[2]), .Opcode5(Opcode[1]),
    .Opcode6(Opcode[0]), .RegWrite(RegWrite), .RegDst(RegDst), .ALUSrc(ALUSrc), .Branch(Branch),
    .MemWrite(MemWrite), .MemToReg(MemToReg), .jump(decoderpt1_1_jump), .link(link));
  DecoderPt2 decoderpt2_1 (
    .Opcode(Opcode[5]), .Opcode2(Opcode[4]), .Opcode3(Opcode[3]), .Opcode4(Opcode[2]), .Opcode5(Opcode[1]),
    .Opcode6(Opcode[0]), .ALUOP0(ALUOp[7]), .ALUOP1(ALUOp[6]), .ALUOP2(ALUOp[5]), .ALUOP3(ALUOp[4]),
    .ALUOP4(ALUOp[3]), .ALUOP5(ALUOp[2]), .ALUOP6(ALUOp[1]), .ALUOP7(ALUOp[0]));
  Multiplexer #(.enable("false")) multiplexer_1 (.in0(decoderpt1_1_jump), .in1(1'b1), .out(jump), .sel(and_1_out));
  and and_1 (and_1_out, comparator_1_eq, comparator_2_eq);
  ALUControl2 alucontrol2_1 (
    .ALUOP1(ALUOp[1]), .ALUOp2(ALUOp[0]), .Funct1(Funct[5]), .Funct2(Funct[4]), .Funct3(Funct[3]),
    .Funct4(Funct[2]), .Funct5(Funct[1]), .Funct6(Funct[0]), .addiu(ALUOp[7]), .addi(ALUOp[6]),
    .sltiu(ALUOp[5]), .slti(ALUOp[4]), .andi(ALUOp[3]), .ori(ALUOp[2]), .Switch1(ALUControl));
endmodule

module Decoder (
  input  Opcode,
  input  Opcode2,
  input  Opcode3,
  input  Opcode4,
  input  Opcode5,
  input  Opcode6,
  output RegWrite,
  output RegDst,
  output ALUSrc,
  output Branch,
  output MemWrite,
  output MemToReg,
  output ALUOp,
  output ALUOp2
);

  wire and_1_out, and_2_out, not_1_out, not_2_out, not_4_out, not_5_out;

  not not_1 (not_1_out, Opcode3);
  not not_2 (not_2_out, Opcode4);
  not not_3 (RegDst, Opcode5);
  not not_4 (not_4_out, Opcode);
  not not_5 (not_5_out, Opcode4);
  and and_1 (and_1_out, not_1_out, not_2_out);
  and and_2 (and_2_out, Opcode3, Opcode4);
  and and_3 (ALUOp, not_4_out, not_5_out);
  or or_1 (RegWrite, and_1_out, and_2_out);

  assign ALUOp2 = Opcode4;
  assign ALUSrc = Opcode6;
  assign Branch = Opcode4;
  assign MemToReg = Opcode6;
  assign MemWrite = Opcode3;
endmodule

module ALUControl2 (
  input  ALUOP1,
  input  ALUOp2,
  input  Funct1,
  input  Funct2,
  input  Funct3,
  input  Funct4,
  input  Funct5,
  input  Funct6,
  input  addiu,
  input  addi,
  input  sltiu,
  input  slti,
  input  andi,
  input  ori,
  output [3:0] Switch1
);

  wire and_1_out, and_2_out, and_3_out, and_4_out, and_5_out, and_6_out, and_7_out, and_8_out, and_9_out,
       and_10_out, and_11_out, and_12_out, and_13_out, not_1_out, not_2_out, not_3_out, not_4_out, not_5_out,
       not_6_out, not_7_out, not_8_out, not_9_out, not_10_out, not_11_out, not_12_out, not_13_out,
       not_14_out, not_15_out, not_16_out, not_17_out, or_5_out;
  wire [3:0] multiplexer_1_out, multiplexer_2_out, or_2_out;

  and and_1 (and_1_out, ALUOP1, Funct4, Funct6);
  and and_2 (and_2_out, ALUOP1, Funct4, Funct5);
  and and_3 (and_3_out, ALUOP1, Funct3);
  not not_1 (not_1_out, Funct4);
  not not_2 (not_2_out, Funct5);
  not not_3 (not_3_out, Funct5);
  not not_4 (not_4_out, Funct6);
  not not_5 (not_5_out, Funct3);
  not not_6 (not_6_out, Funct4);
  not not_7 (not_7_out, ALUOP1);
  not not_8 (not_8_out, ALUOp2);
  not not_9 (not_9_out, ALUOp2);
  not not_10 (not_10_out, ALUOp2);
  not not_11 (not_11_out, Funct5);
  not not_12 (not_12_out, Funct6);
  not not_13 (not_13_out, ALUOP1);
  not not_14 (not_14_out, Funct3);
  and and_4 (and_4_out, not_14_out, Funct5, not_15_out);
  not not_15 (not_15_out, Funct6);
  and and_5 (and_5_out, Funct3, Funct6);
  not not_16 (not_16_out, Funct3);
  and and_6 (and_6_out, Funct1, not_16_out, not_17_out);
  not not_17 (not_17_out, Funct6);
  or or_1 (or_2_out[3], and_1_out, and_2_out, and_3_out);
  and and_7 (and_7_out, ALUOP1, not_1_out, not_2_out, Funct6);
  and and_8 (and_8_out, ALUOP1, Funct4, not_3_out, not_4_out);
  and and_9 (and_9_out, ALUOP1, Funct1, not_5_out, not_6_out, Funct5);
  and and_10 (and_10_out, not_7_out, not_8_out);
  and and_11 (and_11_out, not_9_out, Funct5, Funct6);
  and and_12 (and_12_out, not_10_out, Funct1, not_11_out, not_12_out);
  and and_13 (and_13_out, ALUOP1, Funct3);
  or or_2 (or_2_out[0], not_13_out, and_4_out, and_5_out, and_6_out);
  or or_3 (or_2_out[2], ALUOp2, and_7_out, and_8_out, and_9_out);
  or or_4 (or_2_out[1], and_10_out, and_11_out, and_12_out, and_13_out);
  Multiplexer #(.select(5), .width(4)) multiplexer_1 (
    .in0(4'b0000), .in1(4'b0111), .in2(4'b1010), .in3(4'b0000), .in4(4'b1011), .in5(4'b0000), .in6(4'b0000),
    .in7(4'b0000), .in8(4'b0011), .in9(4'b0000), .in10(4'b0000), .in11(4'b0000), .in12(4'b0000),
    .in13(4'b0000), .in14(4'b0000), .in15(4'b0000), .in16(4'b0100), .in17(4'b0000), .in18(4'b0000),
    .in19(4'b0000), .in20(4'b0000), .in21(4'b0000), .in22(4'b0000), .in23(4'b0000), .in24(4'b0000),
    .in25(4'b0000), .in26(4'b0000), .in27(4'b0000), .in28(4'b0000), .in29(4'b0000), .in30(4'b0000),
    .in31(4'b0000), .out(multiplexer_1_out), .sel({addiu, addi, sltiu, slti, andi}));  // open: en
  Multiplexer #(.width(4)) multiplexer_2 (
    .in0(multiplexer_1_out), .in1(4'b1000), .out(multiplexer_2_out), .sel(ori));  // open: en
  Multiplexer #(.width(4), .enable("false")) multiplexer_3 (
    .in0(or_2_out), .in1(multiplexer_2_out), .out(Switch1), .sel(or_5_out));
  or or_5 (or_5_out, addiu, addi, sltiu, slti, andi, ori);
endmodule

module display_control (
  input  [31:0] inval,
  input  [31:0] inval_2,
  input  [31:0] inval_3,
  input  [31:0] inval_4,
  input  write,
  input  write_2,
  input  write_3,
  input  write_4,
  input  [31:0] inval_5,
  input  [31:0] inval_6,
  input  [31:0] inval_7,
  input  [31:0] inval_8,
  input  write_5,
  input  write_6,
  input  write_7,
  input  write_8,
  input  [31:0] inval_9,
  input  [31:0] inval_10,
  input  [31:0] inval_11,
  input  [31:0] inval_12,
  input  write_9,
  input  write_10,
  input  write_11,
  input  write_12,
  input  [31:0] inval_13,
  input  [31:0] inval_14,
  input  [31:0] inval_15,
  input  [31:0] inval_16,
  input  write_13,
  input  write_14,
  input  write_15,
  input  write_16,
  input  [31:0] inval_17,
  input  [31:0] inval_18,
  input  [31:0] inval_19,
  input  [31:0] inval_20,
  input  write_17,
  input  write_18,
  input  write_19,
  input  write_20,
  input  [31:0] inval_21,
  input  [31:0] inval_22,
  input  [31:0] inval_23,
  input  [31:0] inval_24,
  input  write_21,
  input  write_22,
  input  write_23,
  input  write_24,
  input  [31:0] inval_25,
  input  [31:0] inval_26,
  input  [31:0] inval_27,
  input  [31:0] inval_28,
  input  write_25,
  input  write_26,
  input  write_27,
  input  write_28,
  input  [31:0] inval_29,
  input  [31:0] inval_30,
  input  [31:0] inval_31,
  input  [31:0] inval_32,
  input  write_29,
  input  write_30,
  input  write_31,
  input  write_32,
  input  in_65,
  output [31:0] outval,
  output [31:0] outval_2,
  output [31:0] outval_3,
  output [31:0] outval_4,
  output [31:0] outval_5,
  output [31:0] outval_6,
  output [31:0] outval_7,
  output [31:0] outval_8,
  output [31:0] outval_9,
  output [31:0] outval_10,
  output [31:0] outval_11,
  output [31:0] outval_12,
  output [31:0] outval_13,
  output [31:0] outval_14,
  output [31:0] outval_15,
  output [31:0] outval_16,
  output [31:0] outval_17,
  output [31:0] outval_18,
  output [31:0] outval_19,
  output [31:0] outval_20,
  output [31:0] outval_21,
  output [31:0] outval_22,
  output [31:0] outval_23,
  output [31:0] outval_24,
  output [31:0] outval_25,
  output [31:0] outval_26,
  output [31:0] outval_27,
  output [31:0] outval_28,
  output [31:0] outval_29,
  output [31:0] outval_30,
  output [31:0] outval_31,
  output [31:0] outval_32
);

  wire [31:0] multiplexer_1_out, multiplexer_2_out, multiplexer_3_out, multiplexer_4_out, multiplexer_5_out,
       multiplexer_6_out, multiplexer_7_out, multiplexer_8_out, multiplexer_9_out, multiplexer_10_out,
       multiplexer_11_out, multiplexer_12_out, multiplexer_13_out, multiplexer_14_out, multiplexer_15_out,
       multiplexer_16_out, multiplexer_17_out, multiplexer_18_out, multiplexer_19_out, multiplexer_20_out,
       multiplexer_21_out, multiplexer_22_out, multiplexer_23_out, multiplexer_24_out, multiplexer_25_out,
       multiplexer_26_out, multiplexer_27_out, multiplexer_28_out, multiplexer_29_out, multiplexer_30_out,
       multiplexer_31_out, multiplexer_32_out;

  Multiplexer #(.width(32), .enable("false")) multiplexer_1 (
    .in0(outval_4), .in1(inval_4), .out(multiplexer_1_out), .sel(write_4));
  Multiplexer #(.width(32), .enable("false")) multiplexer_2 (
    .in0(outval_8), .in1(inval_8), .out(multiplexer_2_out), .sel(write_8));
  Multiplexer #(.width(32), .enable("false")) multiplexer_3 (
    .in0(outval_12), .in1(inval_12), .out(multiplexer_3_out), .sel(write_12));
  Multiplexer #(.width(32), .enable("false")) multiplexer_4 (
    .in0(outval_16), .in1(inval_16), .out(multiplexer_4_out), .sel(write_16));
  Multiplexer #(.width(32), .enable("false")) multiplexer_5 (
    .in0(outval_20), .in1(inval_20), .out(multiplexer_5_out), .sel(write_20));
  Multiplexer #(.width(32), .enable("false")) multiplexer_6 (
    .in0(outval_24), .in1(inval_24), .out(multiplexer_6_out), .sel(write_24));
  Multiplexer #(.width(32), .enable("false")) multiplexer_7 (
    .in0(outval_28), .in1(inval_28), .out(multiplexer_7_out), .sel(write_28));
  Multiplexer #(.width(32), .enable("false")) multiplexer_8 (
    .in0(outval_32), .in1(inval_32), .out(multiplexer_8_out), .sel(write_32));
  Register #(.width(32)) register_1 (.D(multiplexer_1_out), .Q(outval_4), .clr(in_65));  // open: en, clk
  Register #(.width(32)) register_2 (.D(multiplexer_2_out), .Q(outval_8), .clr(in_65));  // open: en, clk
  Register #(.width(32)) register_3 (.D(multiplexer_3_out), .Q(outval_12), .clr(in_65));  // open: en, clk
  Register #(.width(32)) register_4 (.D(multiplexer_4_out), .Q(outval_16), .clr(in_65));  // open: en, clk
  Register #(.width(32)) register_5 (.D(multiplexer_5_out), .Q(outval_20), .clr(in_65));  // open: en, clk
  Register #(.width(32)) register_6 (.D(multiplexer_6_out), .Q(outval_24), .clr(in_65));  // open: en, clk
  Register #(.width(32)) register_7 (.D(multiplexer_7_out), .Q(outval_28), .clr(in_65));  // open: en, clk
  Register #(.width(32)) register_8 (.D(multiplexer_8_out), .Q(outval_32), .clr(in_65));  // open: en, clk
  Multiplexer #(.width(32), .enable("false")) multiplexer_9 (
    .in0(outval_3), .in1(inval_3), .out(multiplexer_9_out), .sel(write_3));
  Multiplexer #(.width(32), .enable("false")) multiplexer_10 (
    .in0(outval_7), .in1(inval_7), .out(multiplexer_10_out), .sel(write_7));
  Multiplexer #(.width(32), .enable("false")) multiplexer_11 (
    .in0(outval_11), .in1(inval_11), .out(multiplexer_11_out), .sel(write_11));
  Multiplexer #(.width(32), .enable("false")) multiplexer_12 (
    .in0(outval_15), .in1(inval_15), .out(multiplexer_12_out), .sel(write_15));
  Multiplexer #(.width(32), .enable("false")) multiplexer_13 (
    .in0(outval_19), .in1(inval_19), .out(multiplexer_13_out), .sel(write_19));
  Multiplexer #(.width(32), .enable("false")) multiplexer_14 (
    .in0(outval_23), .in1(inval_23), .out(multiplexer_14_out), .sel(write_23));
  Multiplexer #(.width(32), .enable("false")) multiplexer_15 (
    .in0(outval_27), .in1(inval_27), .out(multiplexer_15_out), .sel(write_27));
  Multiplexer #(.width(32), .enable("false")) multiplexer_16 (
    .in0(outval_31), .in1(inval_31), .out(multiplexer_16_out), .sel(write_31));
  Register #(.width(32)) register_9 (.D(multiplexer_9_out), .Q(outval_3), .clr(in_65));  // open: en, clk
  Register #(.width(32)) register_10 (.D(multiplexer_10_out), .Q(outval_7), .clr(in_65));  // open: en, clk
  Register #(.width(32)) register_11 (.D(multiplexer_11_out), .Q(outval_11), .clr(in_65));  // open: en, clk
  Register #(.width(32)) register_12 (.D(multiplexer_12_out), .Q(outval_15), .clr(in_65));  // open: en, clk
  Register #(.width(32)) register_13 (.D(multiplexer_13_out), .Q(outval_19), .clr(in_65));  // open: en, clk
  Register #(.width(32)) register_14 (.D(multiplexer_14_out), .Q(outval_23), .clr(in_65));  // open: en, clk
  Register #(.width(32)) register_15 (.D(multiplexer_15_out), .Q(outval_27), .clr(in_65));  // open: en, clk
  Register #(.width(32)) register_16 (.D(multiplexer_16_out), .Q(outval_31), .clr(in_65));  // open: en, clk
  Multiplexer #(.width(32), .enable("false")) multiplexer_17 (
    .in0(outval_2), .in1(inval_2), .out(multiplexer_17_out), .sel(write_2));
  Register #(.width(32)) register_17 (.D(multiplexer_17_out), .Q(outval_2), .clr(in_65));  // open: en, clk
  Multiplexer #(.width(32), .enable("false")) multiplexer_18 (
    .in0(outval_6), .in1(inval_6), .out(multiplexer_18_out), .sel(write_6));
  Register #(.width(32)) register_18 (.D(multiplexer_18_out), .Q(outval_6), .clr(in_65));  // open: en, clk
  Multiplexer #(.width(32), .enable("false")) multiplexer_19 (
    .in0(outval_10), .in1(inval_10), .out(multiplexer_19_out), .sel(write_10));
  Register #(.width(32)) register_19 (.D(multiplexer_19_out), .Q(outval_10), .clr(in_65));  // open: en, clk
  Multiplexer #(.width(32), .enable("false")) multiplexer_20 (
    .in0(outval_14), .in1(inval_14), .out(multiplexer_20_out), .sel(write_14));
  Register #(.width(32)) register_20 (.D(multiplexer_20_out), .Q(outval_14), .clr(in_65));  // open: en, clk
  Register #(.width(32)) register_21 (.D(multiplexer_21_out), .Q(outval_18), .clr(in_65));  // open: en, clk
  Multiplexer #(.width(32), .enable("false")) multiplexer_21 (
    .in0(outval_18), .in1(inval_18), .out(multiplexer_21_out), .sel(write_18));
  Multiplexer #(.width(32), .enable("false")) multiplexer_22 (
    .in0(outval_22), .in1(inval_22), .out(multiplexer_22_out), .sel(write_22));
  Register #(.width(32)) register_22 (.D(multiplexer_22_out), .Q(outval_22), .clr(in_65));  // open: en, clk
  Register #(.width(32)) register_23 (.D(multiplexer_23_out), .Q(outval_26), .clr(in_65));  // open: en, clk
  Multiplexer #(.width(32), .enable("false")) multiplexer_23 (
    .in0(outval_26), .in1(inval_26), .out(multiplexer_23_out), .sel(write_26));
  Register #(.width(32)) register_24 (.D(multiplexer_24_out), .Q(outval_30), .clr(in_65));  // open: en, clk
  Multiplexer #(.width(32), .enable("false")) multiplexer_24 (
    .in0(outval_30), .in1(inval_30), .out(multiplexer_24_out), .sel(write_30));
  Multiplexer #(.width(32), .enable("false")) multiplexer_25 (
    .in0(outval), .in1(inval), .out(multiplexer_25_out), .sel(write));
  Multiplexer #(.width(32), .enable("false")) multiplexer_26 (
    .in0(outval_5), .in1(inval_5), .out(multiplexer_26_out), .sel(write_5));
  Multiplexer #(.width(32), .enable("false")) multiplexer_27 (
    .in0(outval_9), .in1(inval_9), .out(multiplexer_27_out), .sel(write_9));
  Multiplexer #(.width(32), .enable("false")) multiplexer_28 (
    .in0(outval_13), .in1(inval_13), .out(multiplexer_28_out), .sel(write_13));
  Multiplexer #(.width(32), .enable("false")) multiplexer_29 (
    .in0(outval_17), .in1(inval_17), .out(multiplexer_29_out), .sel(write_17));
  Multiplexer #(.width(32), .enable("false")) multiplexer_30 (
    .in0(outval_21), .in1(inval_21), .out(multiplexer_30_out), .sel(write_21));
  Multiplexer #(.width(32), .enable("false")) multiplexer_31 (
    .in0(outval_25), .in1(inval_25), .out(multiplexer_31_out), .sel(write_25));
  Multiplexer #(.width(32), .enable("false")) multiplexer_32 (
    .in0(outval_29), .in1(inval_29), .out(multiplexer_32_out), .sel(write_29));
  Register #(.width(32)) register_25 (.D(multiplexer_25_out), .Q(outval), .clr(in_65));  // open: en, clk
  Register #(.width(32)) register_26 (.D(multiplexer_26_out), .Q(outval_5), .clr(in_65));  // open: en, clk
  Register #(.width(32)) register_27 (.D(multiplexer_27_out), .Q(outval_9), .clr(in_65));  // open: en, clk
  Register #(.width(32)) register_28 (.D(multiplexer_28_out), .Q(outval_13), .clr(in_65));  // open: en, clk
  Register #(.width(32)) register_29 (.D(multiplexer_29_out), .Q(outval_17), .clr(in_65));  // open: en, clk
  Register #(.width(32)) register_30 (.D(multiplexer_30_out), .Q(outval_21), .clr(in_65));  // open: en, clk
  Register #(.width(32)) register_31 (.D(multiplexer_31_out), .Q(outval_25), .clr(in_65));  // open: en, clk
  Register #(.width(32)) register_32 (.D(multiplexer_32_out), .Q(outval_29), .clr(in_65));  // open: en, clk

  // Other names for the same wires on the sheet: clk = in_65
endmodule

module NewDecoder (
  input  Opcode6,
  input  Opcode5,
  input  Opcode4,
  input  Opcode3,
  input  Opcode2,
  input  Opcode,
  output RegDst,
  output ALUSrc,
  output MemToReg,
  output RegWrite,
  output MemRead,
  output MemWrite,
  output Branch,
  output ALUOp1,
  output ALUOp0
);

  and and_1 (ALUOp1, ~Opcode6, ~Opcode5, ~Opcode4, ~Opcode3, ~Opcode2, ~Opcode);  // AND_Gate
  and and_2 (MemRead, Opcode6, ~Opcode5, ~Opcode4, ~Opcode3, Opcode2, Opcode);  // AND_Gate
  and and_3 (MemWrite, Opcode6, ~Opcode5, Opcode4, ~Opcode3, Opcode2, Opcode);  // AND_Gate
  and and_4 (ALUOp0, ~Opcode6, ~Opcode5, ~Opcode4, Opcode3, ~Opcode2, ~Opcode);  // AND_Gate
  or or_1 (ALUSrc, MemRead, MemWrite);
  or or_2 (RegWrite, ALUOp1, MemRead);

  assign Branch = ALUOp0;
  assign MemToReg = MemRead;
  assign RegDst = ALUOp1;
endmodule

module DecoderPt1 (
  input  Opcode,
  input  Opcode2,
  input  Opcode3,
  input  Opcode4,
  input  Opcode5,
  input  Opcode6,
  output RegWrite,
  output RegDst,
  output ALUSrc,
  output Branch,
  output MemWrite,
  output MemToReg,
  output jump,
  output link
);

  wire and_1_out, and_2_out, and_3_out, and_4_out, and_5_out, and_6_out, and_7_out, and_8_out, and_9_out,
       and_10_out, and_11_out, and_12_out, and_13_out, and_14_out, and_15_out, and_16_out, and_17_out,
       and_18_out, and_19_out, and_20_out, and_21_out, and_22_out, and_23_out, and_24_out, and_25_out,
       not_1_out, not_2_out, not_3_out, not_4_out, not_5_out, not_6_out, not_7_out, not_8_out, not_9_out,
       not_10_out, not_11_out, not_12_out, not_13_out, not_14_out, not_15_out, not_16_out, not_17_out,
       not_18_out, not_19_out, not_20_out, not_21_out, not_22_out, not_23_out, not_24_out, not_25_out,
       not_26_out, not_27_out, not_28_out, not_29_out, not_30_out, not_31_out, not_32_out, not_33_out;

  not not_1 (not_1_out, Opcode3);
  not not_2 (not_2_out, Opcode4);
  not not_3 (not_3_out, Opcode5);
  not not_4 (not_4_out, Opcode3);
  not not_5 (not_5_out, Opcode4);
  not not_6 (not_6_out, Opcode);
  not not_7 (not_7_out, Opcode2);
  not not_8 (not_8_out, Opcode3);
  not not_9 (not_9_out, Opcode4);
  not not_10 (not_10_out, Opcode3);
  not not_11 (not_11_out, Opcode4);
  not not_12 (not_12_out, Opcode3);
  not not_13 (not_13_out, Opcode5);
  not not_14 (not_14_out, Opcode5);
  not not_15 (not_15_out, Opcode5);
  not not_16 (not_16_out, Opcode);
  not not_17 (not_17_out, Opcode2);
  not not_18 (not_18_out, Opcode4);
  not not_19 (not_19_out, Opcode);
  not not_20 (not_20_out, Opcode2);
  not not_21 (not_21_out, Opcode5);
  not not_22 (not_22_out, Opcode);
  not not_23 (not_23_out, Opcode2);
  not not_24 (not_24_out, Opcode3);
  not not_25 (not_25_out, Opcode3);
  not not_26 (not_26_out, Opcode6);
  not not_27 (not_27_out, Opcode6);
  not not_28 (not_28_out, Opcode3);
  not not_29 (not_29_out, Opcode);
  not not_30 (not_30_out, Opcode3);
  not not_31 (not_31_out, Opcode);
  not not_32 (not_32_out, Opcode3);
  not not_33 (not_33_out, Opcode4);
  and and_1 (and_1_out, not_1_out, not_2_out, not_3_out);
  and and_2 (and_2_out, not_4_out, not_5_out, Opcode6);
  and and_3 (and_3_out, not_6_out, not_7_out, Opcode3);
  and and_4 (and_4_out, Opcode3, Opcode4);
  and and_5 (and_5_out, Opcode2, not_8_out, not_9_out);
  and and_6 (and_6_out, Opcode, not_10_out, not_11_out);
  and and_7 (and_7_out, not_12_out, not_13_out);
  and and_8 (and_8_out, Opcode2, not_14_out);
  and and_9 (and_9_out, Opcode, not_15_out);
  and and_10 (and_10_out, not_16_out, not_17_out, not_18_out, Opcode5);
  and and_11 (and_11_out, Opcode5, Opcode6);
  and and_12 (and_12_out, not_19_out, not_20_out, Opcode3, not_21_out);
  and and_13 (and_13_out, Opcode2, Opcode6);
  and and_14 (and_14_out, Opcode, Opcode6);
  and and_15 (and_15_out, not_22_out, not_23_out, not_24_out, Opcode6);
  and and_16 (and_16_out, not_25_out, Opcode4);
  and and_17 (and_17_out, Opcode4, Opcode5, not_26_out);
  and and_18 (and_18_out, Opcode2, Opcode4);
  and and_19 (and_19_out, Opcode, Opcode4);
  and and_20 (and_20_out, Opcode3, Opcode4, Opcode5, not_27_out);
  and and_21 (and_21_out, Opcode2, Opcode3);
  and and_22 (and_22_out, Opcode, Opcode3);
  and and_23 (and_23_out, not_28_out, Opcode6);
  and and_24 (and_24_out, Opcode2, Opcode6);
  and and_25 (and_25_out, Opcode, Opcode6);
  and and_26 (jump, not_29_out, not_30_out, Opcode5);
  and and_27 (link, not_31_out, not_32_out, not_33_out, Opcode6);
  or or_1 (RegWrite, and_1_out, and_2_out, and_3_out, and_4_out, and_5_out, and_6_out);
  or or_2 (RegDst, and_7_out, and_8_out, and_9_out);
  or or_3 (ALUSrc, and_10_out, and_11_out, and_12_out, and_13_out, and_14_out);
  or or_4 (Branch, and_15_out, and_16_out, and_17_out, and_18_out, and_19_out);
  or or_5 (MemWrite, and_20_out, and_21_out, and_22_out);
  or or_6 (MemToReg, and_23_out, and_24_out, and_25_out);
endmodule

module DecoderPt2 (
  input  Opcode,
  input  Opcode2,
  input  Opcode3,
  input  Opcode4,
  input  Opcode5,
  input  Opcode6,
  output ALUOP0,
  output ALUOP1,
  output ALUOP2,
  output ALUOP3,
  output ALUOP4,
  output ALUOP5,
  output ALUOP6,
  output ALUOP7
);

  wire and_7_out, and_8_out, and_9_out, and_10_out, and_11_out, and_12_out, not_1_out, not_2_out, not_3_out,
       not_4_out, not_5_out, not_6_out, not_7_out, not_8_out, not_9_out, not_10_out, not_11_out, not_12_out,
       not_13_out, not_14_out, not_15_out, not_16_out, not_17_out, not_18_out, not_19_out, not_20_out,
       not_21_out, not_22_out, not_23_out, not_24_out, not_25_out, not_26_out, not_27_out, not_28_out,
       not_29_out, not_30_out, not_31_out, not_32_out;

  not not_1 (not_1_out, Opcode);
  not not_2 (not_2_out, Opcode2);
  not not_3 (not_3_out, Opcode4);
  not not_4 (not_4_out, Opcode5);
  not not_5 (not_5_out, Opcode);
  not not_6 (not_6_out, Opcode2);
  not not_7 (not_7_out, Opcode4);
  not not_8 (not_8_out, Opcode5);
  not not_9 (not_9_out, Opcode6);
  not not_10 (not_10_out, Opcode);
  not not_11 (not_11_out, Opcode2);
  not not_12 (not_12_out, Opcode4);
  not not_13 (not_13_out, Opcode);
  not not_14 (not_14_out, Opcode2);
  not not_15 (not_15_out, Opcode4);
  not not_16 (not_16_out, Opcode6);
  not not_17 (not_17_out, Opcode);
  not not_18 (not_18_out, Opcode2);
  not not_19 (not_19_out, Opcode5);
  not not_20 (not_20_out, Opcode6);
  not not_21 (not_21_out, Opcode);
  not not_22 (not_22_out, Opcode2);
  not not_23 (not_23_out, Opcode5);
  not not_24 (not_24_out, Opcode3);
  not not_25 (not_25_out, Opcode4);
  not not_26 (not_26_out, Opcode6);
  not not_27 (not_27_out, Opcode);
  not not_28 (not_28_out, Opcode4);
  not not_29 (not_29_out, Opcode5);
  not not_30 (not_30_out, Opcode3);
  not not_31 (not_31_out, Opcode5);
  not not_32 (not_32_out, Opcode3);
  and and_1 (ALUOP0, not_1_out, not_2_out, Opcode3, not_3_out, not_4_out, Opcode6);
  and and_2 (ALUOP1, not_5_out, not_6_out, Opcode3, not_7_out, not_8_out, not_9_out);
  and and_3 (ALUOP2, not_10_out, not_11_out, Opcode3, not_12_out, Opcode5, Opcode6);
  and and_4 (ALUOP3, not_13_out, not_14_out, Opcode3, not_15_out, Opcode5, not_16_out);
  and and_5 (ALUOP4, not_17_out, not_18_out, Opcode3, Opcode4, not_19_out, not_20_out);
  and and_6 (ALUOP5, not_21_out, not_22_out, Opcode3, Opcode4, not_23_out, Opcode6);
  and and_7 (and_7_out, not_24_out, not_25_out, not_26_out);
  and and_8 (and_8_out, not_27_out, not_28_out, Opcode5);
  and and_9 (and_9_out, Opcode3, Opcode4, not_29_out);
  and and_10 (and_10_out, Opcode3, Opcode4, Opcode6);
  and and_11 (and_11_out, not_30_out, not_31_out, Opcode6);
  and and_12 (and_12_out, not_32_out, Opcode4);
  or or_1 (ALUOP6, and_7_out, and_8_out, and_9_out, and_10_out);
  or or_2 (ALUOP7, and_11_out, and_12_out);
endmodule

module comparator (
  input  [5:0] opcode,
  input  [31:0] alu1,
  input  [31:0] alu2,
  output do_branch
);

  wire comparator_1_eq, comparator_2_eq, comparator_2_gt, not_1_out, or_1_out;

  Comparator #(.width(32)) comparator_1 (.a(alu1), .b(alu2), .eq(comparator_1_eq));  // open: gt, lt
  Comparator #(.width(32)) comparator_2 (
    .a(alu1), .b({32{1'b0}}), .gt(comparator_2_gt), .eq(comparator_2_eq));  // open: lt
  or or_1 (or_1_out, comparator_2_gt, comparator_2_eq);
  not not_1 (not_1_out, comparator_1_eq);
  Pull_Resistor pull_resistor_1 (.node(do_branch));
  Multiplexer #(.select(3), .enable("false")) multiplexer_1 (
    .in1(or_1_out), .in4(comparator_1_eq), .in5(not_1_out), .out(do_branch), .sel(opcode[2:0]));  // open: in0, in2, in3, in6, in7
endmodule

module logical (
  input  opcode1,
  input  opcode2,
  input  opcode3,
  input  opcode4,
  input  opcode5,
  input  opcode6,
  output logical
);

  wire and_1_out, and_2_out, not_1_out, not_2_out, not_3_out, not_4_out, not_5_out, not_6_out;

  not not_1 (not_1_out, opcode1);
  not not_2 (not_2_out, opcode5);
  not not_3 (not_3_out, opcode6);
  not not_4 (not_4_out, opcode2);
  not not_5 (not_5_out, opcode5);
  not not_6 (not_6_out, opcode6);
  and and_1 (and_1_out, not_1_out, opcode3, opcode4, not_2_out, not_3_out);
  and and_2 (and_2_out, not_4_out, opcode3, opcode4, not_5_out, not_6_out);
  or or_1 (logical, and_1_out, and_2_out);
endmodule
