// Logisim project interesting_io.circ as structural Verilog: 1 circuit, main circuit main
module main (
  output [31:0] s0_Value,
  output [31:0] s1_Value,
  output [31:0] s2_Value,
  output [31:0] ra_Value,
  output [31:0] sp_Value,
  output [31:0] Time_Step,
  output [31:0] Requested_Address,
  output [31:0] Requested_Instruction,
  output halt
);

  wire clock_1_out, nor_1_out;

  // Probe on s0_Value
  Clock clock_1 (.out(clock_1_out));
  cpu_main main_1 (
    .INSTRUCTION(Requested_Instruction), .CLOCK(clock_1_out), .FETCH_ADDRESS(Requested_Address),
    .s0_Value(s0_Value), .s1_Value(s1_Value), .s2_Value(s2_Value), .ra_Value(ra_Value), .sp_Value(sp_Value));
  Counter #(.width(32), .max('hffffffff)) counter_1 (
    .Q(Time_Step), .clk(clock_1_out));  // open: load, D, count, carry, clr
  // Probe on s0_Value[6:0]
  Comparator #(.width(32)) comparator_1 (.a(Time_Step), .b(32'h25), .eq(halt));  // open: gt, lt
  // Probe on Requested_Address
  TTY tty_1 (.data(s0_Value[6:0]), .clk(clock_1_out), .we(nor_1_out));  // open: clr
  nor nor_1 (nor_1_out, Requested_Instruction[28], Requested_Instruction[29], Requested_Instruction[30], Requested_Instruction[31]);
  ROM #(.addrWidth(24), .dataWidth(32)) rom_1 (
    .addr(Requested_Address[25:2]), .data(Requested_Instruction));  // open: sel
  // Probe on Requested_Instruction

  // Other names for the same wires on the sheet: fetch_addr[31:0] = Requested_Address;
  //   Instruction[31:0] = Requested_Instruction

  // Notes on the sheet:
  //   YOUR CPU SHOULD FIT IN HERE!
  //   Instruction Memory
  //   contents of rom_1 (hex, n*v repeats v):
  //   3c010000 34210048 18021 3c010000 34210065 18021 3c010000 3421006c 18021 3c010000 3421006c 18021
  //   3c010000 3421006f 18021 3c010000 34210020 18021 3c010000 34210057 18021 3c010000 3421006f 18021
  //   3c010000 34210072 18021 3c010000 3421006c 18021 3c010000 34210064 18021 3c010000 34210021 18021
endmodule
